# Fritzing sketch WeatherStation (saved by Fritzing 0.9.3b)
breadboards: 1

parts:
  U1 = NodeMCU V1.0
  RHT1 = Humidity and Temperature Sensor RHT03
  Part1 = BH1750
  YL-83_-_Detection_Board1 = YL-83 Rain Sensor - Detection Board
  YL-83_-_Control_Board1 = YL-83 Rain Sensor - Control Board
  R2 = Resistor [tolerance=±5% resistance=10k package=THT]
  S1 = Pushbutton [package="[THT]"]

nets:
  N1: U1.D0, U1.RST, S1.Pin_3, S1.Pin_4
  N2: U1.D1, RHT1.Data-signal, R2.Pin_1
  3V3: U1.3V3, Part1.VCC
  N3: U1.D5, Part1.SCL
  N4: U1.D6, Part1.SDA
  N5: U1.D7, YL-83_-_Control_Board1.VCC
  VIN: U1.Vin, RHT1.Vcc, R2.Pin_0
  N6: U1.A0, YL-83_-_Control_Board1.AO
  GND: RHT1.GND_2, Part1.GND, YL-83_-_Control_Board1.GND, S1.Pin_1, S1.Pin_2
  N7: YL-83_-_Detection_Board1.POS, YL-83_-_Control_Board1.POS
  N8: YL-83_-_Detection_Board1.NEG, YL-83_-_Control_Board1.NEG

custom parts:
  NodeMCU V1.0: ESP8266 based NodeMCU
  BH1750: Light Sensor
  YL-83 Rain Sensor - Detection Board: The YL-83 is a rain sensor that has more resistance when dry and less resistance when wet. The module runs at 5V.
  YL-83 Rain Sensor - Control Board: The YL-83 is a rain sensor that has more resistance when dry and less resistance when wet. The module runs at 5V.
